# Fritzing sketch pressure-button-4x4-double (saved by Fritzing 0.8.0b)
breadboards: 1

parts:
  C1 = Ceramic Capacitor [capacitance=100nF package="100 mil [THT, multilayer]"]
  C2 = Ceramic Capacitor [capacitance=100nF package="100 mil [THT, multilayer]"]
  J6 = female pin header, 1 pin [form="♀ (female)"]
  J2 = female pin header, 1 pin [form="♀ (female)"]
  C3 = Ceramic Capacitor [capacitance=100nF package="100 mil [THT, multilayer]"]
  C4 = Ceramic Capacitor [capacitance=100nF package="100 mil [THT, multilayer]"]
  J8 = female pin header, 1 pin [form="♀ (female)"]
  J5 = female pin header, 1 pin [form="♀ (female)"]
  J9 = female pin header, 1 pin [form="♀ (female)"]
  C5 = Ceramic Capacitor [capacitance=100nF package="100 mil [THT, multilayer]"]
  C6 = Ceramic Capacitor [capacitance=100nF package="100 mil [THT, multilayer]"]
  J11 = female pin header, 1 pin [form="♀ (female)" part_number="Vcc 5 V"]
  J12 = female pin header, 1 pin [form="♀ (female)" part_number=Gnd]
  J13 = female pin header, 1 pin [form="♀ (female)"]
  J14 = female pin header, 1 pin [form="♀ (female)"]
  J15 = female pin header, 1 pin [form="♀ (female)"]
  J17 = female pin header, 1 pin [form="♀ (female)"]
  C13 = Ceramic Capacitor [capacitance=100nF package="100 mil [THT, multilayer]"]
  J18 = female pin header, 1 pin [form="♀ (female)"]
  C14 = Ceramic Capacitor [capacitance=100nF package="100 mil [THT, multilayer]"]
  C15 = Ceramic Capacitor [capacitance=100nF package="100 mil [THT, multilayer]"]
  C16 = Ceramic Capacitor [capacitance=100nF package="100 mil [THT, multilayer]"]
  C17 = Ceramic Capacitor [capacitance=100nF package="100 mil [THT, multilayer]"]
  C18 = Ceramic Capacitor [capacitance=100nF package="100 mil [THT, multilayer]"]
  D7 = Rectifier Diode [part_number=1N4001 package="300 mil [THT]"]
  C19 = Ceramic Capacitor [capacitance=100nF package="100 mil [THT, multilayer]"]
  C20 = Ceramic Capacitor [capacitance=100nF package="100 mil [THT, multilayer]"]
  C21 = Ceramic Capacitor [capacitance=100nF package="100 mil [THT, multilayer]"]
  C22 = Ceramic Capacitor [capacitance=100nF package="100 mil [THT, multilayer]"]
  D3 = Rectifier Diode [part_number=1N4001 package="300 mil [THT]"]
  D4 = Rectifier Diode [part_number=1N4001 package="300 mil [THT]"]
  J4 = female pin header, 1 pin [form="♀ (female)"]
  J7 = female pin header, 1 pin [form="♀ (female)"]
  J10 = female pin header, 1 pin [form="♀ (female)"]
  BUTTON27 = Pressure button WS2812b
  BUTTON16 = Pressure button WS2812b
  BUTTON23 = Pressure button WS2812b
  BUTTON14 = Pressure button WS2812b
  BUTTON26 = Pressure button WS2812b
  BUTTON28 = Pressure button WS2812b
  BUTTON22 = Pressure button WS2812b
  BUTTON21 = Pressure button WS2812b
  BUTTON20 = Pressure button WS2812b
  BUTTON17 = Pressure button WS2812b
  BUTTON19 = Pressure button WS2812b
  BUTTON13 = Pressure button WS2812b
  BUTTON15 = Pressure button WS2812b
  BUTTON24 = Pressure button WS2812b
  BUTTON18 = Pressure button WS2812b
  BUTTON25 = Pressure button WS2812b
  J19 = female pin header, 1 pin [form="♀ (female)" part_number="Vcc 5 V B"]
  D14 = Rectifier Diode [part_number=1N4001 package="300 mil [THT]"]
  D15 = Rectifier Diode [part_number=1N4001 package="300 mil [THT]"]
  D2 = Rectifier Diode [part_number=1N4001 package="300 mil [THT]"]
  D5 = Rectifier Diode [part_number=1N4001 package="300 mil [THT]"]
  D6 = Rectifier Diode [part_number=1N4001 package="300 mil [THT]"]
  D10 = Rectifier Diode [part_number=1N4001 package="300 mil [THT]"]
  D16 = Rectifier Diode [part_number=1N4001 package="300 mil [THT]"]
  D9 = Rectifier Diode [part_number=1N4001 package="300 mil [THT]"]
  D8 = Rectifier Diode [part_number=1N4001 package="300 mil [THT]"]
  D11 = Rectifier Diode [part_number=1N4001 package="300 mil [THT]"]
  D12 = Rectifier Diode [part_number=1N4001 package="300 mil [THT]"]
  D13 = Rectifier Diode [part_number=1N4001 package="300 mil [THT]"]
  D17 = Rectifier Diode [part_number=1N4001 package="300 mil [THT]"]

nets:
  GND: C1.0, C4.0, C5.0, J12.pin1, C13.0, BUTTON16.gnd, BUTTON14.gnd, BUTTON13.gnd, BUTTON15.gnd
  VCC: C1.1, C4.1, C5.1, C6.1, J11.pin1, C13.1, C15.1, C19.1, BUTTON16.vcc, BUTTON14.vcc, BUTTON21.vcc, BUTTON20.vcc, BUTTON13.vcc, BUTTON15.vcc, BUTTON25.vcc, J19.pin1
  N1: C2.0, BUTTON18.gnd
  N2: C2.1, BUTTON18.vcc
  N3: J6.pin1, BUTTON16.ba2, BUTTON16.bb2, BUTTON28.ba2, BUTTON28.bb2, BUTTON17.ba2, BUTTON17.bb2, BUTTON24.ba2, BUTTON24.bb2
  N4: J2.pin1, BUTTON27.ba2, BUTTON27.bb2, BUTTON23.ba2, BUTTON23.bb2, BUTTON15.ba2, BUTTON15.bb2, BUTTON18.ba2, BUTTON18.bb2
  N5: C3.0, BUTTON19.gnd
  N6: C3.1, BUTTON19.vcc
  N7: J8.pin1, D15.anode, D2.anode, D5.anode, D6.anode
  N8: J5.pin1, D7.anode, D3.anode, D4.anode, D14.anode
  N9: J9.pin1, BUTTON21.ba2, BUTTON21.bb2, BUTTON20.ba2, BUTTON20.bb2, BUTTON13.ba2, BUTTON13.bb2, BUTTON25.ba2, BUTTON25.bb2
  N10: C6.0, BUTTON20.gnd
  N11: J13.pin1, D10.anode, D16.anode, D9.anode, D8.anode
  N12: J14.pin1, D11.anode, D12.anode, D13.anode, D17.anode
  N13: J15.pin1, BUTTON25.dout
  N14: J17.pin1, BUTTON14.ba2, BUTTON14.bb2, BUTTON26.ba2, BUTTON26.bb2, BUTTON22.ba2, BUTTON22.bb2, BUTTON19.ba2, BUTTON19.bb2
  N15: J18.pin1, BUTTON16.din
  N16: C14.0, BUTTON17.gnd
  N17: C14.1, BUTTON17.vcc
  N18: C15.0, BUTTON21.gnd
  N19: C16.0, BUTTON22.gnd
  N20: C16.1, BUTTON22.vcc
  N21: C17.0, BUTTON23.gnd
  N22: C17.1, BUTTON23.vcc
  N23: C18.0, BUTTON24.gnd
  N24: C18.1, BUTTON24.vcc
  N25: D7.cathode, BUTTON13.ba1, BUTTON13.bb1
  N26: C19.0, BUTTON25.gnd
  N27: C20.0, BUTTON26.gnd
  N28: C20.1, BUTTON26.vcc
  N29: C21.0, BUTTON27.gnd
  N30: C21.1, BUTTON27.vcc
  N31: C22.0, BUTTON28.gnd
  N32: C22.1, BUTTON28.vcc
  N33: D3.cathode, BUTTON15.ba1, BUTTON15.bb1
  N34: D4.cathode, BUTTON14.ba1, BUTTON14.bb1
  N35: J4.pin1, BUTTON15.din
  N36: J7.pin1, BUTTON14.din
  N37: J10.pin1, BUTTON13.din
  N38: BUTTON27.ba1, BUTTON27.bb1, D13.cathode
  N39: BUTTON16.ba1, BUTTON16.bb1, D14.cathode
  N40: BUTTON16.dout, BUTTON17.din
  N41: BUTTON23.ba1, BUTTON23.bb1, D10.cathode
  N42: BUTTON14.dout, BUTTON19.din
  N43: BUTTON26.ba1, BUTTON26.bb1, D12.cathode
  N44: BUTTON28.ba1, BUTTON28.bb1, D17.cathode
  N45: BUTTON22.ba1, BUTTON22.bb1, D9.cathode
  N46: BUTTON21.ba1, BUTTON21.bb1, D8.cathode
  N47: BUTTON21.din, BUTTON20.dout
  N48: BUTTON21.dout, BUTTON25.din
  N49: BUTTON20.ba1, BUTTON20.bb1, D6.cathode
  N50: BUTTON20.din, BUTTON13.dout
  N51: BUTTON17.ba1, BUTTON17.bb1, D15.cathode
  N52: BUTTON19.ba1, BUTTON19.bb1, D5.cathode
  N53: BUTTON15.dout, BUTTON18.din
  N54: BUTTON24.ba1, BUTTON24.bb1, D16.cathode
  N55: BUTTON18.ba1, BUTTON18.bb1, D2.cathode
  N56: BUTTON25.ba1, BUTTON25.bb1, D11.cathode

custom parts:
  Pressure button WS2812b: Pressure button with LED
